// Logisim project HardikHyperionProcessorAndSubtractor.circ as structural Verilog: 3 circuits, main circuit main
module main (
);

  wire CLK, DATA, MOV;
  wire [2:0] OP, Rd;
  wire [2:1] Ra;
  wire [3:0] alu1_1_alu_output, controlled_buffer_1_out, counter_1_q, counter_1_q_2, IMMD, reg1_1_bus_a,
       reg1_1_bus_b;
  wire [15:0] rom_1_data;
  wire [15:9] register_1_q;

  assign controlled_buffer_1_out = MOV ? IMMD : 4'bz;  // Controlled_Buffer controlled_buffer_1
  assign controlled_buffer_1_out = DATA ? alu1_1_alu_output : 4'bz;  // Controlled_Buffer controlled_buffer_2
  Clock clock_1 (.out(CLK));
  Counter counter_1 (
    .clr(1'b0), .load(1'b0), .up(1'b1), .count(1'b1), .clk(CLK), .Q({counter_1_q_2, counter_1_q}));  // open: D, carry
  Hex_Digit_Display hex_digit_display_1 (.value(counter_1_q_2));  // open: dp
  Hex_Digit_Display hex_digit_display_2 (.value(counter_1_q));  // open: dp
  REG1 reg1_1 (
    .INP(controlled_buffer_1_out), .CLK(CLK), .SEL_A({Ra, IMMD[3]}), .SEL_INP(Rd), .SEL_B(IMMD[2:0]),
    .BUS_A(reg1_1_bus_a), .BUS_B(reg1_1_bus_b));
  ROM #(.dataWidth(16)) rom_1 (.addr({counter_1_q_2, counter_1_q}), .data(rom_1_data));
  Register #(.width(16)) register_1 (
    .D(rom_1_data), .en(1'b1), .clk(CLK), .Q({register_1_q[15:14], OP, register_1_q[10:9], Ra, IMMD, Rd}));  // open: clr
  ALU1 alu1_1 (.A(reg1_1_bus_a), .B(reg1_1_bus_b), .OP(OP), .ALU_OUTPUT(alu1_1_alu_output));
  and and_1 (MOV, ~register_1_q[14], ~register_1_q[15]);  // AND_Gate
  and and_2 (DATA, register_1_q[14], register_1_q[15]);

  // Other names for the same wires on the sheet: Rb[2:0] = IMMD[2:0]; Ra[0] = IMMD[3]

  // Notes on the sheet:
  //   contents of rom_1 (hex, n*v repeats v):
  //   28 19 12 c00b e0d6 6666 7777 8888 9999
endmodule

module ALU1 (
  input  [3:0] A,
  input  [3:0] B,
  input  [2:0] OP,
  output [3:0] ALU_OUTPUT
);

  wire [3:0] adder_1_out, and_1_out, or_1_out, subtractor_1_out, xor_1_out;

  Adder #(.width(4)) adder_1 (.a(A), .b(B), .out(adder_1_out), .cin(1'b0));  // open: cout
  assign and_1_out = A & B;  // AND_Gate and_1, 4 bits wide
  assign or_1_out = A | B;  // OR_Gate or_1, 4 bits wide
  assign xor_1_out = A ^ B;  // XOR_Gate xor_1, 4 bits wide
  Subtractor #(.width(4)) subtractor_1 (.a(A), .b(B), .out(subtractor_1_out), .bin(1'b0));  // open: bout
  Multiplexer #(.select(3), .width(4)) multiplexer_1 (
    .in0(adder_1_out), .in1(and_1_out), .in2(or_1_out), .in3(xor_1_out), .in4(subtractor_1_out),
    .out(ALU_OUTPUT), .sel(OP));  // open: in5, in6, in7
endmodule

module REG1 (
  input  [3:0] INP,
  input  CLK,
  input  [2:0] SEL_A,
  input  [2:0] SEL_INP,
  input  [2:0] SEL_B,
  output [3:0] BUS_A,
  output [3:0] BUS_B
);

  wire demultiplexer_1_out0, demultiplexer_1_out1, demultiplexer_1_out2, demultiplexer_1_out3,
       demultiplexer_1_out4, demultiplexer_1_out5, demultiplexer_1_out6, demultiplexer_1_out7;
  wire [3:0] R0_q, R1_q, R2_q, R3_q, R4_q, R5_q, R6_q, R7_q;

  Demultiplexer #(.select(3)) demultiplexer_1 (
    .out0(demultiplexer_1_out0), .out1(demultiplexer_1_out1), .out2(demultiplexer_1_out2),
    .out3(demultiplexer_1_out3), .out4(demultiplexer_1_out4), .out5(demultiplexer_1_out5),
    .out6(demultiplexer_1_out6), .out7(demultiplexer_1_out7), .in(1'b1), .sel(SEL_INP));
  Register #(.width(4)) R0 (.D(INP), .en(demultiplexer_1_out0), .clk(CLK), .Q(R0_q), .clr(1'b0));
  Register #(.width(4)) R1 (.D(INP), .en(demultiplexer_1_out1), .clk(CLK), .Q(R1_q), .clr(1'b0));
  Register #(.width(4)) R2 (.D(INP), .en(demultiplexer_1_out2), .clk(CLK), .Q(R2_q), .clr(1'b0));
  Register #(.width(4)) R3 (.D(INP), .en(demultiplexer_1_out3), .clk(CLK), .Q(R3_q), .clr(1'b0));
  Register #(.width(4)) R4 (.D(INP), .en(demultiplexer_1_out4), .clk(CLK), .Q(R4_q), .clr(1'b0));
  Register #(.width(4)) R5 (.D(INP), .en(demultiplexer_1_out5), .clk(CLK), .Q(R5_q), .clr(1'b0));
  Register #(.width(4)) R6 (.D(INP), .en(demultiplexer_1_out6), .clk(CLK), .Q(R6_q), .clr(1'b0));
  Register #(.width(4)) R7 (.D(INP), .en(demultiplexer_1_out7), .clk(CLK), .Q(R7_q), .clr(1'b0));
  Multiplexer #(.select(3), .width(4)) multiplexer_1 (
    .in0(R0_q), .in1(R1_q), .in2(R2_q), .in3(R3_q), .in4(R4_q), .in5(R5_q), .in6(R6_q), .in7(R7_q),
    .out(BUS_A), .sel(SEL_A));
  Multiplexer #(.select(3), .width(4)) multiplexer_2 (
    .in0(R0_q), .in1(R1_q), .in2(R2_q), .in3(R3_q), .in4(R4_q), .in5(R5_q), .in6(R6_q), .in7(R7_q),
    .out(BUS_B), .sel(SEL_B));
endmodule
